# Fritzing sketch NodeMCU Dual DS18B20 (saved by Fritzing 0.9.3b)
breadboards: 1

parts:
  U1 = NodeMCU V1.0
  R1 = Resistor [tolerance=±5% resistance=3.3k package=THT]
  DS1 = DS18B20 1-Wire Temperature Sensor [part_number=DS18B20]
  DS2 = DS18B20 1-Wire Temperature Sensor [part_number=DS18B20]

nets:
  N1: U1.D4, R1.Pin_1, DS1.DQ, DS2.DQ
  VDD: U1.3V3, R1.Pin_0, DS1.VDD, DS2.VDD
  GND: U1.GND, DS1.GND, DS2.GND

custom parts:
  NodeMCU V1.0: ESP8266 based NodeMCU
